// Digital circuit p01 diagrams.dig as structural Verilog
module p01_diagrams (
  input  in_1,
  output out_2
);

  nand nand_1 (out_2, in_1, in_1);

  // Notes on the sheet:
  //   Not Gate
endmodule
